// Logisim project Group5_PartA.circ as structural Verilog: 10 circuits, main circuit Reg16bit
module Reg16bit (
  input  clk,
  input  Reset,
  input  OE,
  input  WE,
  input  [15:0] Din,
  output [15:0] Dout,
  output [15:0] Result,
  output [7:0] LSB,
  output [7:0] MSB
);

  Register #(.width(16)) register_1 (.D(Din), .en(WE), .clk(clk), .Q(Result), .clr(Reset));
  assign Dout = OE ? Result : 16'bz;  // Controlled_Buffer controlled_buffer_1
  BitSelector #(.group(8), .width(16)) bitselector_1 (.in(Result), .out(LSB), .sel(1'b0));
  BitSelector #(.group(8), .width(16)) bitselector_2 (.in(Result), .out(MSB), .sel(1'b1));

  // Notes on the sheet:
  //   constant value 0x0
  //   constant value 0x1
endmodule

module project_ro (
  input  [15:0] A,
  input  [15:0] B,
  input  [2:0] RU_Selector,
  output RU_Result
);

  wire comparator_1_eq, comparator_1_gt, comparator_1_lt, not_1_out, or_1_out, or_2_out;

  Comparator #(.width(16)) comparator_1 (
    .a(A), .b(B), .gt(comparator_1_gt), .eq(comparator_1_eq), .lt(comparator_1_lt));
  or or_1 (or_1_out, comparator_1_gt, comparator_1_eq);
  or or_2 (or_2_out, comparator_1_lt, comparator_1_eq);
  not not_1 (not_1_out, comparator_1_eq);
  Multiplexer #(.select(3)) multiplexer_1 (
    .in0(comparator_1_gt), .in1(comparator_1_eq), .in2(or_1_out), .in3(comparator_1_lt), .in4(or_2_out),
    .in5(not_1_out), .out(RU_Result), .sel(RU_Selector));  // open: in6, in7

  // Notes on the sheet:
  //   >
  //   >=
  //   <
  //   <=
  //   ==
  //   !-
endmodule

module project_ao (
  input  [15:0] A,
  input  [15:0] B,
  input  [3:0] in_3,
  output [15:0] out_4
);

  wire [15:0] adder_1_out, and_1_out, divider_1_out, divider_1_rem, multiplier_1_out, negator_1_out,
       negator_2_out, or_1_out, shifter_1_out, shifter_2_out, shifter_3_out, shifter_4_out, subtractor_1_out,
       xor_1_out;

  Adder #(.width(16)) adder_1 (.a(A), .b(B), .out(adder_1_out));  // open: cin, cout
  assign and_1_out = A & B;  // AND_Gate and_1, 16 bits wide
  assign or_1_out = A | B;  // OR_Gate or_1, 16 bits wide
  assign xor_1_out = A ^ B;  // XOR_Gate xor_1, 16 bits wide
  Divider #(.width(16)) divider_1 (.a(A), .b(B), .out(divider_1_out), .rem(divider_1_rem));  // open: upper
  Multiplier #(.width(16)) multiplier_1 (.a(A), .b(B), .out(multiplier_1_out));  // open: cin, cout
  Subtractor #(.width(16)) subtractor_1 (.a(A), .b(B), .out(subtractor_1_out));  // open: bin, bout
  Shifter #(.width(16)) shifter_1 (.in(A), .\dist (4'b0010), .out(shifter_1_out));
  Shifter #(.width(16)) shifter_2 (.in(B), .\dist (4'b0010), .out(shifter_2_out));
  Shifter #(.width(16)) shifter_3 (.in(A), .\dist (4'b0010), .out(shifter_3_out));
  Shifter #(.width(16)) shifter_4 (.in(B), .\dist (4'b0010), .out(shifter_4_out));
  Negator #(.width(16)) negator_1 (.in(A), .out(negator_1_out));
  Negator #(.width(16)) negator_2 (.in(B), .out(negator_2_out));
  Multiplexer #(.select(4), .width(16)) multiplexer_1 (
    .in0(adder_1_out), .in1(and_1_out), .in2(or_1_out), .in3(xor_1_out), .in4(divider_1_out),
    .in5(divider_1_rem), .in6(multiplier_1_out), .in7(subtractor_1_out), .in8(shifter_1_out),
    .in9(shifter_2_out), .in10(shifter_3_out), .in11(shifter_4_out), .in12(negator_1_out),
    .in13(negator_2_out), .out(out_4), .sel(in_3));  // open: in14, in15

  // Notes on the sheet:
  //   16-BIT AU
endmodule

module project_alu (
  input  [15:0] A,
  input  [15:0] B,
  input  OE,
  input  [3:0] AU_selector,
  input  [2:0] RU_Selector,
  output [15:0] AU_Result,
  output [15:0] AU_Dout,
  output RU_Result
);

  project_ao project_ao_1 (.A(A), .B(B), .in_3(AU_selector), .out_4(AU_Result));
  project_ro project_ro_1 (.A(A), .B(B), .RU_Selector(RU_Selector), .RU_Result(RU_Result));
  assign AU_Dout = OE ? AU_Result : 16'bz;  // Controlled_Buffer controlled_buffer_1

  // Notes on the sheet:
  //   16 BITS ALU
endmodule

module Datapath (
  input  in_1,
  input  in_2,
  input  [15:0] test_data1,
  input  in_4,
  input  in_5,
  input  in_6,
  input  in_7,
  input  in_8,
  input  in_9,
  input  in_10,
  input  in_11,
  input  in_12,
  input  in_13,
  input  in_14,
  input  [3:0] AU_SELECTOR,
  input  [2:0] RU_SELECTOR,
  input  in_17,
  input  in_18,
  output [7:0] out_19,
  output [15:0] out_20,
  output [15:0] out_21,
  output [15:0] out_22,
  output [15:0] out_23,
  output [15:0] out_24,
  output [15:0] out_25
);

  wire clock_1_out;
  wire [7:0] bitselector_1_out, MAR_dout;
  wire [15:0] ALU_au_dout, IR_dout;

  Clock clock_1 (.out(clock_1_out));
  BitSelector #(.group(8), .width(16)) bitselector_1 (.in(IR_dout), .out(bitselector_1_out), .sel(1'b1));
  Reg16bit IR (
    .clk(clock_1_out), .OE(in_6), .WE(in_8), .Din(ALU_au_dout), .Dout(IR_dout), .Result(out_20));  // open: Reset, LSB, MSB
  Reg16bit A (
    .clk(clock_1_out), .OE(in_10), .WE(in_11), .Din(ALU_au_dout), .Result(out_22));  // open: Reset, Dout, LSB, MSB
  Reg16bit B (
    .clk(clock_1_out), .OE(in_17), .WE(in_18), .Din(ALU_au_dout), .Result(out_25));  // open: Reset, Dout, LSB, MSB
  project_alu ALU (
    .A(out_22), .B(out_25), .OE(in_13), .AU_selector(AU_SELECTOR), .RU_Selector(RU_SELECTOR),
    .AU_Result(out_23), .AU_Dout(ALU_au_dout));  // open: RU_Result
  LED led_1 (.in(ALU_au_dout[15]));
  LED led_2 (.in(ALU_au_dout[14]));
  LED led_3 (.in(ALU_au_dout[13]));
  LED led_4 (.in(ALU_au_dout[12]));
  assign ALU_au_dout = in_4 ? test_data1 : 16'bz;  // Controlled_Buffer controlled_buffer_1
  LED led_5 (.in(ALU_au_dout[11]));
  LED led_6 (.in(ALU_au_dout[10]));
  LED led_7 (.in(ALU_au_dout[9]));
  LED led_8 (.in(ALU_au_dout[8]));
  LED led_9 (.in(ALU_au_dout[7]));
  LED led_10 (.in(ALU_au_dout[6]));
  LED led_11 (.in(ALU_au_dout[5]));
  LED led_12 (.in(ALU_au_dout[4]));
  LED led_13 (.in(ALU_au_dout[3]));
  LED led_14 (.in(ALU_au_dout[2]));
  LED led_15 (.in(ALU_au_dout[1]));
  LED led_16 (.in(ALU_au_dout[0]));
  assign ALU_au_dout = in_5 ? ALU_au_dout : 16'bz;  // Controlled_Buffer controlled_buffer_2
  Reg16bit Output_Register (
    .clk(clock_1_out), .OE(in_12), .WE(in_14), .Din(ALU_au_dout), .Dout(ALU_au_dout), .Result(out_24));  // open: Reset, LSB, MSB
  Reg8bit MAR (
    .clk(clock_1_out), .OE(in_1), .WE(in_2), .Din(bitselector_1_out), .Dout(MAR_dout), .Result(out_19));  // open: Reset
  Reg16bit MBR (
    .clk(clock_1_out), .OE(in_7), .WE(in_9), .Din(ALU_au_dout), .Dout(ALU_au_dout), .Result(out_21));  // open: Reset, LSB, MSB
  LED led_17 (.in(ALU_au_dout[15]));
  LED led_18 (.in(ALU_au_dout[14]));
  LED led_19 (.in(ALU_au_dout[13]));
  LED led_20 (.in(ALU_au_dout[12]));
  LED led_21 (.in(ALU_au_dout[11]));
  LED led_22 (.in(ALU_au_dout[10]));
  LED led_23 (.in(ALU_au_dout[9]));
  LED led_24 (.in(ALU_au_dout[8]));
  LED led_25 (.in(ALU_au_dout[7]));
  LED led_26 (.in(ALU_au_dout[6]));
  LED led_27 (.in(ALU_au_dout[5]));
  LED led_28 (.in(ALU_au_dout[4]));
  LED led_29 (.in(ALU_au_dout[3]));
  LED led_30 (.in(ALU_au_dout[2]));
  LED led_31 (.in(ALU_au_dout[1]));
  LED led_32 (.in(ALU_au_dout[0]));

  // Notes on the sheet:
  //   INTERNAL ADDRESS BUS
  //   INTERNAL DATA BUS
  //   EXTERNAL ADDRESS BUS
  //   EXTERNAL DATA BUS
endmodule

module cpu2 (
  input  in_1,
  input  [3:0] in_2,
  input  [7:0] Test_data,
  input  OE,
  input  [1:0] AU_SELECTOR,
  input  [2:0] LU_SELECTOR,
  output [3:0] out_7,
  output [3:0] counter_content,
  output [7:0] out_9,
  output [7:0] out_10,
  output [7:0] out_11,
  output [7:0] out_12,
  output COUT,
  output [7:0] AU_RESULT,
  output ALU_RESULT,
  output [2:0] SC_O
);

  wire A_p2, alu_1_p3, alu_1_p4, B_p2, CLK_out, cu_1_p8, cu_1_p9, cu_1_p10, cu_1_p11, cu_1_p13, IR_p2, IR_p3,
       MAR_p2, MAR_p3, MBR_p2, MBR_p3, OUTPUT_REGISTER_p2, OUTPUT_REGISTER_p3;
  wire [3:0] bitselector_2_out, controlled_buffer_1_out, decimal_decoder_1_p1_3, decimal_decoder_2_p1_3,
       decimal_decoder_4_p2_3, MAR_p5;
  wire [7:0] bit_extender_1_out, bit_extender_2_out, IR_p4, IR_p6, ram_1_dout;
  wire [15:0] decimal_decoder_1_p1, decimal_decoder_2_p1, decimal_decoder_3_p2, decimal_decoder_3_p2_2,
       decimal_decoder_4_p2, decimal_decoder_5_p2, decimal_decoder_5_p2_2;
  wire [27:16] decimal_decoder_1_p1_2, decimal_decoder_2_p1_2, decimal_decoder_4_p2_2;

  Clock CLK (.out(CLK_out));
  Counter #(.max('h3), .width(4)) PC (
    .count(cu_1_p9), .clk(CLK_out), .D(controlled_buffer_1_out), .Q(counter_content));  // open: clr, load, up, carry
  // reg8bits IR: pin names not known; wires that end beside it: CLK_out, IR_p2, IR_p3, IR_p4, out_9, IR_p6
  assign controlled_buffer_1_out = cu_1_p8 ? counter_content : 4'bz;  // Controlled_Buffer controlled_buffer_1
  // reg8bits A: pin names not known; wires that end beside it: CLK_out, A_p2, IR_p4, out_11, out_11
  // ALU alu_1: pin names not known; wires that end beside it: AU_SELECTOR, out_11, alu_1_p3, alu_1_p4, LU_SELECTOR, COUT, AU_RESULT, IR_p4, ALU_RESULT
  // reg8bits B: pin names not known; wires that end beside it: CLK_out, B_p2, IR_p4, alu_1_p4, alu_1_p4
  BitSelector #(.group(4)) bitselector_1 (.in(IR_p6), .out(controlled_buffer_1_out), .sel(1'b0));
  assign bit_extender_1_out = {{4{1'b0}}, counter_content};  // Bit_Extender bit_extender_1
  // Decimal_Decoder decimal_decoder_1: pin names not known; wires that end beside it: {decimal_decoder_1_p1_3, decimal_decoder_1_p1_2, decimal_decoder_1_p1}
  _7_Segment_Display u_7_segment_display_1 (
    .g(decimal_decoder_1_p1[15]), .f(decimal_decoder_1_p1[14]), .a(decimal_decoder_1_p1[13]),
    .b(decimal_decoder_1_p1[12]), .e(decimal_decoder_1_p1_3[3]), .d(decimal_decoder_1_p1_3[2]),
    .c(decimal_decoder_1_p1_3[1]), .dp(decimal_decoder_1_p1_3[0]));
  _7_Segment_Display u_7_segment_display_2 (
    .g(decimal_decoder_1_p1[11]), .f(decimal_decoder_1_p1[10]), .a(decimal_decoder_1_p1[9]),
    .b(decimal_decoder_1_p1[8]), .e(decimal_decoder_1_p1_2[27]), .d(decimal_decoder_1_p1_2[26]),
    .c(decimal_decoder_1_p1_2[25]), .dp(decimal_decoder_1_p1_2[24]));
  // Decimal_Decoder decimal_decoder_2: pin names not known; wires that end beside it: {decimal_decoder_2_p1_3, decimal_decoder_2_p1_2, decimal_decoder_2_p1}
  _7_Segment_Display u_7_segment_display_3 (
    .g(decimal_decoder_2_p1[15]), .f(decimal_decoder_2_p1[14]), .a(decimal_decoder_2_p1[13]),
    .b(decimal_decoder_2_p1[12]), .e(decimal_decoder_2_p1_3[3]), .d(decimal_decoder_2_p1_3[2]),
    .c(decimal_decoder_2_p1_3[1]), .dp(decimal_decoder_2_p1_3[0]));
  _7_Segment_Display u_7_segment_display_4 (
    .g(decimal_decoder_2_p1[11]), .f(decimal_decoder_2_p1[10]), .a(decimal_decoder_2_p1[9]),
    .b(decimal_decoder_2_p1[8]), .e(decimal_decoder_2_p1_2[27]), .d(decimal_decoder_2_p1_2[26]),
    .c(decimal_decoder_2_p1_2[25]), .dp(decimal_decoder_2_p1_2[24]));
  // Decimal_Decoder decimal_decoder_3: pin names not known; wires that end beside it: bit_extender_1_out, {decimal_decoder_3_p2_2, decimal_decoder_3_p2}
  _7_Segment_Display u_7_segment_display_5 (
    .g(decimal_decoder_3_p2[3]), .f(decimal_decoder_3_p2[2]), .a(decimal_decoder_3_p2[1]),
    .b(decimal_decoder_3_p2[0]), .e(decimal_decoder_3_p2_2[3]), .d(decimal_decoder_3_p2_2[2]),
    .c(decimal_decoder_3_p2_2[1]), .dp(decimal_decoder_3_p2_2[0]));
  _7_Segment_Display u_7_segment_display_6 (
    .g(decimal_decoder_1_p1[7]), .f(decimal_decoder_1_p1[6]), .a(decimal_decoder_1_p1[5]),
    .b(decimal_decoder_1_p1[4]), .e(decimal_decoder_1_p1_2[23]), .d(decimal_decoder_1_p1_2[22]),
    .c(decimal_decoder_1_p1_2[21]), .dp(decimal_decoder_1_p1_2[20]));
  _7_Segment_Display u_7_segment_display_7 (
    .g(decimal_decoder_2_p1[7]), .f(decimal_decoder_2_p1[6]), .a(decimal_decoder_2_p1[5]),
    .b(decimal_decoder_2_p1[4]), .e(decimal_decoder_2_p1_2[23]), .d(decimal_decoder_2_p1_2[22]),
    .c(decimal_decoder_2_p1_2[21]), .dp(decimal_decoder_2_p1_2[20]));
  LED led_1 (.in(IR_p4[7]));
  assign IR_p4 = OE ? Test_data : 8'bz;  // Controlled_Buffer controlled_buffer_2
  _7_Segment_Display u_7_segment_display_8 (
    .g(decimal_decoder_1_p1[3]), .f(decimal_decoder_1_p1[2]), .a(decimal_decoder_1_p1[1]),
    .b(decimal_decoder_1_p1[0]), .e(decimal_decoder_1_p1_2[19]), .d(decimal_decoder_1_p1_2[18]),
    .c(decimal_decoder_1_p1_2[17]), .dp(decimal_decoder_1_p1_2[16]));
  _7_Segment_Display u_7_segment_display_9 (
    .g(decimal_decoder_2_p1[3]), .f(decimal_decoder_2_p1[2]), .a(decimal_decoder_2_p1[1]),
    .b(decimal_decoder_2_p1[0]), .e(decimal_decoder_2_p1_2[19]), .d(decimal_decoder_2_p1_2[18]),
    .c(decimal_decoder_2_p1_2[17]), .dp(decimal_decoder_2_p1_2[16]));
  LED led_2 (.in(IR_p4[6]));
  LED led_3 (.in(IR_p4[5]));
  LED led_4 (.in(IR_p4[4]));
  LED led_5 (.in(IR_p4[3]));
  LED led_6 (.in(IR_p4[2]));
  LED led_7 (.in(IR_p4[1]));
  LED led_8 (.in(IR_p4[0]));
  assign IR_p4 = cu_1_p13 ? out_10 : 8'bz;  // Controlled_Buffer controlled_buffer_3
  // reg4bits MAR: pin names not known; wires that end beside it: controlled_buffer_1_out, MAR_p2, MAR_p3, CLK_out, MAR_p5, out_7
  Counter #(.max('h5), .width(3)) STEP_COUNTER (.clk(CLK_out), .Q(SC_O));  // open: clr, load, up, count, D, carry
  _7_Segment_Display u_7_segment_display_10 (
    .g(decimal_decoder_4_p2[15]), .f(decimal_decoder_4_p2[14]), .a(decimal_decoder_4_p2[13]),
    .b(decimal_decoder_4_p2[12]), .e(decimal_decoder_4_p2_3[3]), .d(decimal_decoder_4_p2_3[2]),
    .c(decimal_decoder_4_p2_3[1]), .dp(decimal_decoder_4_p2_3[0]));
  BitSelector #(.group(4)) bitselector_2 (.in(out_9), .out(bitselector_2_out), .sel(1'b1));
  // reg8bits MBR: pin names not known; wires that end beside it: CLK_out, MBR_p2, MBR_p3, IR_p4, out_10, IR_p4
  // reg8bits OUTPUT_REGISTER: pin names not known; wires that end beside it: CLK_out, OUTPUT_REGISTER_p2, OUTPUT_REGISTER_p3, IR_p4, out_12, IR_p4
  // Decimal_Decoder decimal_decoder_4: pin names not known; wires that end beside it: out_12, {decimal_decoder_4_p2_3, decimal_decoder_4_p2_2, decimal_decoder_4_p2}
  _7_Segment_Display u_7_segment_display_11 (
    .g(decimal_decoder_4_p2[11]), .f(decimal_decoder_4_p2[10]), .a(decimal_decoder_4_p2[9]),
    .b(decimal_decoder_4_p2[8]), .e(decimal_decoder_4_p2_2[27]), .d(decimal_decoder_4_p2_2[26]),
    .c(decimal_decoder_4_p2_2[25]), .dp(decimal_decoder_4_p2_2[24]));
  _7_Segment_Display u_7_segment_display_12 (
    .g(decimal_decoder_4_p2[7]), .f(decimal_decoder_4_p2[6]), .a(decimal_decoder_4_p2[5]),
    .b(decimal_decoder_4_p2[4]), .e(decimal_decoder_4_p2_2[23]), .d(decimal_decoder_4_p2_2[22]),
    .c(decimal_decoder_4_p2_2[21]), .dp(decimal_decoder_4_p2_2[20]));
  _7_Segment_Display u_7_segment_display_13 (
    .g(decimal_decoder_4_p2[3]), .f(decimal_decoder_4_p2[2]), .a(decimal_decoder_4_p2[1]),
    .b(decimal_decoder_4_p2[0]), .e(decimal_decoder_4_p2_2[19]), .d(decimal_decoder_4_p2_2[18]),
    .c(decimal_decoder_4_p2_2[17]), .dp(decimal_decoder_4_p2_2[16]));
  assign bit_extender_2_out = {{5{1'b0}}, SC_O};  // Bit_Extender bit_extender_2
  assign MAR_p5 = in_1 ? in_2 : 4'bz;  // Controlled_Buffer controlled_buffer_4
  LED led_9 (.in(IR_p4[7]));
  LED led_10 (.in(IR_p4[6]));
  LED led_11 (.in(IR_p4[5]));
  // CU cu_1: pin names not known; wires that end beside it: bitselector_2_out[3], bitselector_2_out[2], bitselector_2_out[1], bitselector_2_out[0], SC_O[2], SC_O[1], SC_O[0], cu_1_p8, cu_1_p9, cu_1_p10, cu_1_p11, MBR_p3, cu_1_p13, MBR_p2, IR_p3, IR_p2, MAR_p2
  // Decimal_Decoder decimal_decoder_5: pin names not known; wires that end beside it: bit_extender_2_out, {decimal_decoder_5_p2_2, decimal_decoder_5_p2}, MAR_p3, alu_1_p3, A_p2, B_p2, OUTPUT_REGISTER_p2, OUTPUT_REGISTER_p3
  LED led_12 (.in(IR_p4[4]));
  _7_Segment_Display u_7_segment_display_14 (
    .g(decimal_decoder_5_p2[3]), .f(decimal_decoder_5_p2[2]), .a(decimal_decoder_5_p2[1]),
    .b(decimal_decoder_5_p2[0]), .e(decimal_decoder_5_p2_2[3]), .d(decimal_decoder_5_p2_2[2]),
    .c(decimal_decoder_5_p2_2[1]), .dp(decimal_decoder_5_p2_2[0]));
  LED led_13 (.in(IR_p4[3]));
  LED led_14 (.in(IR_p4[2]));
  LED led_15 (.in(IR_p4[1]));
  LED led_16 (.in(IR_p4[0]));
  RAM #(.addrWidth(4), .enables("line")) ram_1 (
    .addr(MAR_p5), .we(cu_1_p10), .clk(CLK_out), .din(IR_p4), .dout(ram_1_dout));
  assign IR_p4 = cu_1_p11 ? ram_1_dout : 8'bz;  // Controlled_Buffer controlled_buffer_5

  // Notes on the sheet:
  //   OE
  //   WE
  //   INTERNAL ADDRESS BUS
  //   D7
  //   D5
  //   D6
  //   D4
  //   D3
  //   D2
  //   D1
  //   OE
  //   WE
  //   INTERNAL DATA BUS
  //   D0
  //   EXTERNAL ADDRESS BUS
  //   oe_test
  //   D7
  //   D5
  //   D6
  //   D4
  //   D3
  //   D2
  //   D1
  //   WE
  //   EXTERNAL DATA BUS
  //   D0
  //   OE
endmodule

module Reg8bit (
  input  clk,
  input  Reset,
  input  OE,
  input  WE,
  input  [7:0] Din,
  output [7:0] Dout,
  output [7:0] Result
);

  Register register_1 (.D(Din), .en(WE), .clk(clk), .Q(Result), .clr(Reset));
  assign Dout = OE ? Result : 8'bz;  // Controlled_Buffer controlled_buffer_1
endmodule

module CPU_2 (
  input  [7:0] in_1,
  input  [15:0] test_data1,
  input  in_3,
  input  in_4,
  input  in_5,
  input  [3:0] AU_SELECTOR,
  input  [2:0] RU_SELECTOR,
  input  in_8,
  output [7:0] out_9,
  output [15:0] out_10,
  output [15:0] out_11,
  output [15:0] out_12,
  output [15:0] out_13,
  output [15:0] out_14,
  output [15:0] out_15
);

  wire clock_1_out, cu_2_1_c0, cu_2_1_c1, cu_2_1_c2, cu_2_1_c3, cu_2_1_c4, cu_2_1_c5, cu_2_1_c6, cu_2_1_c7,
       cu_2_1_c8, cu_2_1_c9, cu_2_1_c10, cu_2_1_c11, cu_2_1_c12, cu_2_1_c13, cu_2_1_c14, cu_2_1_c15;
  wire [2:0] counter_1_q;
  wire [3:0] controlled_buffer_1_out, dec_decoder_1_dout_2, dec_decoder_1_dout_3, dec_decoder_1_dout_4,
       dec_decoder_1_dout_5, dec_decoder_2_dout_2, dec_decoder_2_dout_3, dec_decoder_3_dout_2,
       dec_decoder_3_dout_3, dec_decoder_4_dout_2, dec_decoder_4_dout_3, dec_decoder_5_dout_2,
       dec_decoder_5_dout_3, Program_Counter_q, undriven;
  wire [7:0] bit_extender_2_out, bitselector_2_out, MAR_dout;
  wire [15:0] ALU_au_dout, bit_extender_1_out, bit_extender_4_out, dec_decoder_1_dout, IR_dout, ram_1_dout;
  wire [27:0] dec_decoder_2_dout, dec_decoder_3_dout, dec_decoder_4_dout, dec_decoder_5_dout;

  Clock clock_1 (.out(clock_1_out));
  Counter #(.max('h3), .width(4)) Program_Counter (
    .count(cu_2_1_c1), .clk(clock_1_out), .D(undriven), .Q(Program_Counter_q));  // open: clr, load, up, carry
  assign controlled_buffer_1_out = cu_2_1_c0 ? Program_Counter_q : 4'bz;  // Controlled_Buffer controlled_buffer_1
  assign bit_extender_1_out = {{12{Program_Counter_q[3]}}, Program_Counter_q};  // Bit_Extender bit_extender_1
  _7_Segment_Display u_7_segment_display_1 (
    .g(dec_decoder_1_dout[3]), .f(dec_decoder_1_dout[2]), .a(dec_decoder_1_dout[1]),
    .b(dec_decoder_1_dout[0]), .e(dec_decoder_1_dout_2[3]), .d(dec_decoder_1_dout_2[2]),
    .c(dec_decoder_1_dout_2[1]), .dp(dec_decoder_1_dout_2[0]));
  assign bit_extender_2_out = {{4{controlled_buffer_1_out[3]}}, controlled_buffer_1_out};  // Bit_Extender bit_extender_2
  DEC_DECODER dec_decoder_1 (
    .Din(bit_extender_1_out),
    .Dout({dec_decoder_1_dout_5, dec_decoder_1_dout_4, dec_decoder_1_dout_3, dec_decoder_1_dout_2, dec_decoder_1_dout}));
  Reg16bit IR (
    .clk(clock_1_out), .OE(cu_2_1_c8), .WE(cu_2_1_c7), .Din(ALU_au_dout), .Dout(IR_dout), .Result(out_10));  // open: Reset, LSB, MSB
  DEC_DECODER dec_decoder_2 (
    .Din(out_12),
    .Dout({dec_decoder_2_dout_3, dec_decoder_2_dout[27:16], dec_decoder_2_dout_2, dec_decoder_2_dout[11:0]}));
  _7_Segment_Display u_7_segment_display_2 (
    .g(dec_decoder_2_dout_2[3]), .f(dec_decoder_2_dout_2[2]), .a(dec_decoder_2_dout_2[1]),
    .b(dec_decoder_2_dout_2[0]), .e(dec_decoder_2_dout_3[3]), .d(dec_decoder_2_dout_3[2]),
    .c(dec_decoder_2_dout_3[1]), .dp(dec_decoder_2_dout_3[0]));
  _7_Segment_Display u_7_segment_display_3 (
    .g(dec_decoder_2_dout[11]), .f(dec_decoder_2_dout[10]), .a(dec_decoder_2_dout[9]),
    .b(dec_decoder_2_dout[8]), .e(dec_decoder_2_dout[27]), .d(dec_decoder_2_dout[26]),
    .c(dec_decoder_2_dout[25]), .dp(dec_decoder_2_dout[24]));
  DEC_DECODER dec_decoder_3 (
    .Din(out_15),
    .Dout({dec_decoder_3_dout_3, dec_decoder_3_dout[27:16], dec_decoder_3_dout_2, dec_decoder_3_dout[11:0]}));
  _7_Segment_Display u_7_segment_display_4 (
    .g(dec_decoder_3_dout_2[3]), .f(dec_decoder_3_dout_2[2]), .a(dec_decoder_3_dout_2[1]),
    .b(dec_decoder_3_dout_2[0]), .e(dec_decoder_3_dout_3[3]), .d(dec_decoder_3_dout_3[2]),
    .c(dec_decoder_3_dout_3[1]), .dp(dec_decoder_3_dout_3[0]));
  _7_Segment_Display u_7_segment_display_5 (
    .g(dec_decoder_3_dout[11]), .f(dec_decoder_3_dout[10]), .a(dec_decoder_3_dout[9]),
    .b(dec_decoder_3_dout[8]), .e(dec_decoder_3_dout[27]), .d(dec_decoder_3_dout[26]),
    .c(dec_decoder_3_dout[25]), .dp(dec_decoder_3_dout[24]));
  assign bit_extender_2_out = {{4{undriven[3]}}, undriven};  // Bit_Extender bit_extender_3
  BitSelector #(.group(8), .width(16)) bitselector_1 (.in(IR_dout), .out(bit_extender_2_out), .sel(1'b0));
  _7_Segment_Display u_7_segment_display_6 (
    .g(dec_decoder_2_dout[7]), .f(dec_decoder_2_dout[6]), .a(dec_decoder_2_dout[5]),
    .b(dec_decoder_2_dout[4]), .e(dec_decoder_2_dout[23]), .d(dec_decoder_2_dout[22]),
    .c(dec_decoder_2_dout[21]), .dp(dec_decoder_2_dout[20]));
  _7_Segment_Display u_7_segment_display_7 (
    .g(dec_decoder_2_dout[3]), .f(dec_decoder_2_dout[2]), .a(dec_decoder_2_dout[1]),
    .b(dec_decoder_2_dout[0]), .e(dec_decoder_2_dout[19]), .d(dec_decoder_2_dout[18]),
    .c(dec_decoder_2_dout[17]), .dp(dec_decoder_2_dout[16]));
  _7_Segment_Display u_7_segment_display_8 (
    .g(dec_decoder_3_dout[7]), .f(dec_decoder_3_dout[6]), .a(dec_decoder_3_dout[5]),
    .b(dec_decoder_3_dout[4]), .e(dec_decoder_3_dout[23]), .d(dec_decoder_3_dout[22]),
    .c(dec_decoder_3_dout[21]), .dp(dec_decoder_3_dout[20]));
  _7_Segment_Display u_7_segment_display_9 (
    .g(dec_decoder_3_dout[3]), .f(dec_decoder_3_dout[2]), .a(dec_decoder_3_dout[1]),
    .b(dec_decoder_3_dout[0]), .e(dec_decoder_3_dout[19]), .d(dec_decoder_3_dout[18]),
    .c(dec_decoder_3_dout[17]), .dp(dec_decoder_3_dout[16]));
  Reg16bit A (
    .clk(clock_1_out), .OE(in_5), .WE(cu_2_1_c12), .Din(ALU_au_dout), .Result(out_12));  // open: Reset, Dout, LSB, MSB
  Reg16bit B (
    .clk(clock_1_out), .OE(in_8), .WE(cu_2_1_c13), .Din(ALU_au_dout), .Result(out_15));  // open: Reset, Dout, LSB, MSB
  project_alu ALU (
    .A(out_12), .B(out_15), .OE(cu_2_1_c11), .AU_selector(AU_SELECTOR), .RU_Selector(RU_SELECTOR),
    .AU_Result(out_14), .AU_Dout(ALU_au_dout));  // open: RU_Result
  LED led_1 (.in(ALU_au_dout[15]));
  LED led_2 (.in(ALU_au_dout[14]));
  LED led_3 (.in(ALU_au_dout[13]));
  assign ALU_au_dout = in_4 ? test_data1 : 16'bz;  // Controlled_Buffer controlled_buffer_2
  LED led_4 (.in(ALU_au_dout[12]));
  LED led_5 (.in(ALU_au_dout[11]));
  LED led_6 (.in(ALU_au_dout[10]));
  LED led_7 (.in(ALU_au_dout[9]));
  LED led_8 (.in(ALU_au_dout[8]));
  LED led_9 (.in(ALU_au_dout[7]));
  LED led_10 (.in(ALU_au_dout[6]));
  LED led_11 (.in(ALU_au_dout[5]));
  LED led_12 (.in(ALU_au_dout[4]));
  LED led_13 (.in(ALU_au_dout[3]));
  LED led_14 (.in(ALU_au_dout[2]));
  LED led_15 (.in(ALU_au_dout[1]));
  LED led_16 (.in(ALU_au_dout[0]));
  assign ALU_au_dout = cu_2_1_c5 ? out_11 : 16'bz;  // Controlled_Buffer controlled_buffer_3
  Reg16bit Output_Register (
    .clk(clock_1_out), .OE(cu_2_1_c14), .WE(cu_2_1_c15), .Din(ALU_au_dout), .Dout(ALU_au_dout),
    .Result(out_13));  // open: Reset, LSB, MSB
  DEC_DECODER dec_decoder_4 (
    .Din(out_13),
    .Dout({dec_decoder_4_dout_3, dec_decoder_4_dout[27:16], dec_decoder_4_dout_2, dec_decoder_4_dout[11:0]}));
  _7_Segment_Display u_7_segment_display_10 (
    .g(dec_decoder_4_dout_2[3]), .f(dec_decoder_4_dout_2[2]), .a(dec_decoder_4_dout_2[1]),
    .b(dec_decoder_4_dout_2[0]), .e(dec_decoder_4_dout_3[3]), .d(dec_decoder_4_dout_3[2]),
    .c(dec_decoder_4_dout_3[1]), .dp(dec_decoder_4_dout_3[0]));
  _7_Segment_Display u_7_segment_display_11 (
    .g(dec_decoder_4_dout[11]), .f(dec_decoder_4_dout[10]), .a(dec_decoder_4_dout[9]),
    .b(dec_decoder_4_dout[8]), .e(dec_decoder_4_dout[27]), .d(dec_decoder_4_dout[26]),
    .c(dec_decoder_4_dout[25]), .dp(dec_decoder_4_dout[24]));
  Reg8bit MAR (
    .clk(clock_1_out), .OE(cu_2_1_c10), .WE(cu_2_1_c9), .Din(bit_extender_2_out), .Dout(MAR_dout),
    .Result(out_9));  // open: Reset
  Reg16bit MBR (
    .clk(clock_1_out), .OE(cu_2_1_c6), .WE(cu_2_1_c4), .Din(ALU_au_dout), .Dout(ALU_au_dout), .Result(out_11));  // open: Reset, LSB, MSB
  _7_Segment_Display u_7_segment_display_12 (
    .g(dec_decoder_4_dout[7]), .f(dec_decoder_4_dout[6]), .a(dec_decoder_4_dout[5]),
    .b(dec_decoder_4_dout[4]), .e(dec_decoder_4_dout[23]), .d(dec_decoder_4_dout[22]),
    .c(dec_decoder_4_dout[21]), .dp(dec_decoder_4_dout[20]));
  _7_Segment_Display u_7_segment_display_13 (
    .g(dec_decoder_4_dout[3]), .f(dec_decoder_4_dout[2]), .a(dec_decoder_4_dout[1]),
    .b(dec_decoder_4_dout[0]), .e(dec_decoder_4_dout[19]), .d(dec_decoder_4_dout[18]),
    .c(dec_decoder_4_dout[17]), .dp(dec_decoder_4_dout[16]));
  Counter #(.max('h5), .width(3)) counter_1 (
    .clk(clock_1_out), .Q(counter_1_q));  // open: clr, load, up, count, D, carry
  LED led_17 (.in(ALU_au_dout[15]));
  LED led_18 (.in(ALU_au_dout[14]));
  BitSelector #(.group(8), .width(16)) bitselector_2 (.in(out_10), .out(bitselector_2_out), .sel(1'b1));
  LED led_19 (.in(ALU_au_dout[13]));
  LED led_20 (.in(ALU_au_dout[12]));
  LED led_21 (.in(ALU_au_dout[11]));
  assign MAR_dout = in_3 ? in_1 : 8'bz;  // Controlled_Buffer controlled_buffer_4
  LED led_22 (.in(ALU_au_dout[10]));
  LED led_23 (.in(ALU_au_dout[9]));
  LED led_24 (.in(ALU_au_dout[8]));
  assign bit_extender_4_out = {{13{1'b0}}, counter_1_q};  // Bit_Extender bit_extender_4
  LED led_25 (.in(ALU_au_dout[7]));
  LED led_26 (.in(ALU_au_dout[6]));
  LED led_27 (.in(ALU_au_dout[5]));
  LED led_28 (.in(ALU_au_dout[4]));
  LED led_29 (.in(ALU_au_dout[3]));
  RAM #(.dataWidth(16), .enables("line")) ram_1 (
    .addr(MAR_dout), .we(cu_2_1_c2), .clk(clock_1_out), .din(ALU_au_dout), .dout(ram_1_dout));
  LED led_30 (.in(ALU_au_dout[2]));
  LED led_31 (.in(ALU_au_dout[1]));
  LED led_32 (.in(ALU_au_dout[0]));
  CU_2 cu_2_1 (
    .OPC7(bitselector_2_out[7]), .OPC6(bitselector_2_out[6]), .OPC5(bitselector_2_out[5]),
    .OPC4(bitselector_2_out[4]), .OPC3(bitselector_2_out[3]), .OPC2(bitselector_2_out[2]),
    .OPC1(bitselector_2_out[1]), .OPC0(bitselector_2_out[0]), .SC2(counter_1_q[2]), .SC1(counter_1_q[1]),
    .SC0(counter_1_q[0]), .C0(cu_2_1_c0), .C1(cu_2_1_c1), .C2(cu_2_1_c2), .C3(cu_2_1_c3), .C4(cu_2_1_c4),
    .C5(cu_2_1_c5), .C6(cu_2_1_c6), .C7(cu_2_1_c7), .C8(cu_2_1_c8), .C9(cu_2_1_c9), .C10(cu_2_1_c10),
    .C11(cu_2_1_c11), .C12(cu_2_1_c12), .C13(cu_2_1_c13), .C14(cu_2_1_c14), .C15(cu_2_1_c15));
  DEC_DECODER dec_decoder_5 (
    .Din(bit_extender_4_out),
    .Dout({dec_decoder_5_dout_3, dec_decoder_5_dout[27:16], dec_decoder_5_dout_2, dec_decoder_5_dout[11:0]}));
  _7_Segment_Display u_7_segment_display_14 (
    .g(dec_decoder_5_dout[3]), .f(dec_decoder_5_dout[2]), .a(dec_decoder_5_dout[1]),
    .b(dec_decoder_5_dout[0]), .e(dec_decoder_5_dout[19]), .d(dec_decoder_5_dout[18]),
    .c(dec_decoder_5_dout[17]), .dp(dec_decoder_5_dout[16]));
  assign ALU_au_dout = cu_2_1_c3 ? ram_1_dout : 16'bz;  // Controlled_Buffer controlled_buffer_5

  // Notes on the sheet:
  //   INTERNAL ADDRESS BUS
  //   INTERNAL DATA BUS
  //   EXTERNAL ADDRESS BUS
  //   EXTERNAL DATA BUS
endmodule

module DEC_DECODER (
  input  [15:0] Din,
  output [31:0] Dout
);

  ROM #(.addrWidth(16), .dataWidth(32)) rom_1 (
    .addr(Din),
    .data({Dout[31:28], Dout[15:12], Dout[27:24], Dout[11:8], Dout[23:20], Dout[7:4], Dout[19:16], Dout[3:0]}));

  // Notes on the sheet:
  //   contents of rom_1 (hex, n*v repeats v):
  //   e7 21 cb 6b 2d 6e ee 23 ef 2f 21e7 2121 21cb 216b 212d 216e 21ee 2123 21ef 212f cbe7 cb21 cbcb cb6b
  //   cb2d cb6e cbee cb23 cbef cb2f 6be7 6b21 6bcb 6b6b 6b2d 6b6e 6bee 6b23 6bef 6b2f 2de7 2d21 2dcb 2d6b
  //   2d2d 2d6e 2dee 2d23 2def 2d2f 6ee7 6e21 6ecb 6e6b 6e2d 6e6e 6eee 6e23 6eef 6e2f eee7 ee21 eecb ee6b
  //   ee2d ee6e eeee ee23 eeef ee2f 23e7 2321 23cb 236b 232d 236e 23ee 2323 23ef 232f efe7 ef21 efcb ef6b
  //   ef2d ef6e efee ef23 efef ef2f 2fe7 2f21 2fcb 2f6b 2f2d 2f6e 2fee 2f23 2fef 2f2f 21e7e7 21e721 21e7cb
  //   21e76b 21e72d 21e76e 21e7ee 21e723 21e7ef 21e72f 2121e7 212121 2121cb 21216b 21212d 21216e 2121ee
  //   212123 2121ef 21212f 21cbe7 21cb21 21cbcb 21cb6b 21cb2d 21cb6e 21cbee 21cb23 21cbef 21cb2f 216be7
  //   216b21 216bcb 216b6b 216b2d 216b6e 216bee 216b23 216bef 216b2f 212de7 212d21 212dcb 212d6b 212d2d
  //   212d6e 212dee 212d23 212def 212d2f 216ee7 216e21 216ecb 216e6b 216e2d 216e6e 216eee 216e23 216eef
  //   216e2f 21eee7 21ee21 21eecb 21ee6b 21ee2d 21ee6e 21eeee 21ee23 21eeef 21ee2f 2123e7 212321 2123cb
  //   21236b 21232d 21236e 2123ee 212323 2123ef 21232f 21efe7 21ef21 21efcb 21ef6b 21ef2d 21ef6e 21efee
  //   21ef23 21efef 21ef2f 212fe7 212f21 212fcb 212f6b 212f2d 212f6e 212fee 212f23 212fef 212f2f cbe7e7
  //   cbe721 cbe7cb cbe76b cbe72d cbe76e cbe7ee cbe723 cbe7ef cbe72f cb21e7 cb2121 cb21cb cb216b cb212d
  //   cb216e cb21ee cb2123 cb21ef cb212f cbcbe7 cbcb21 cbcbcb cbcb6b cbcb2d cbcb6e cbcbee cbcb23 cbcbef
  //   cbcb2f cb6be7 cb6b21 cb6bcb cb6b6b cb6b2d cb6b6e cb6bee cb6b23 cb6bef cb6b2f cb2de7 cb2d21 cb2dcb
  //   cb2d6b cb2d2d cb2d6e cb2dee cb2d23 cb2def cb2d2f cb6ee7 cb6e21 cb6ecb cb6e6b cb6e2d cb6e6e
endmodule

module CU_2 (
  input  OPC7,
  input  OPC6,
  input  OPC5,
  input  OPC4,
  input  OPC3,
  input  OPC2,
  input  OPC1,
  input  OPC0,
  input  SC2,
  input  SC1,
  input  SC0,
  output C0,
  output C1,
  output C2,
  output C3,
  output C4,
  output C5,
  output C6,
  output C7,
  output C8,
  output C9,
  output C10,
  output C11,
  output C12,
  output C13,
  output C14,
  output C15
);

  wire and_4_out, and_5_out, and_6_out, and_7_out, and_8_out, and_9_out, and_10_out, and_13_out, and_14_out,
       and_15_out, and_16_out, and_17_out, and_18_out, and_19_out, not_1_out, not_2_out, not_3_out,
       not_4_out, not_5_out;

  not not_1 (not_1_out, OPC1);
  not not_2 (not_2_out, OPC0);
  not not_3 (not_3_out, SC2);
  not not_4 (not_4_out, SC1);
  not not_5 (not_5_out, SC0);
  and and_1 (C0, not_3_out, not_4_out, not_5_out);
  and and_2 (C1, not_3_out, not_4_out, SC0);
  and and_3 (C2, OPC1, SC2);
  and and_4 (and_4_out, not_3_out, not_4_out, SC0);
  and and_5 (and_5_out, not_1_out, SC2, not_5_out);
  and and_6 (and_6_out, not_3_out, not_4_out, SC0);
  and and_7 (and_7_out, OPC1, OPC0, SC0);
  and and_8 (and_8_out, not_1_out, SC2, not_5_out);
  and and_9 (and_9_out, SC1, not_5_out);
  and and_10 (and_10_out, SC2, SC0);
  and and_11 (C6, OPC1, SC2);
  and and_12 (C7, SC1, not_5_out);
  and and_13 (and_13_out, not_1_out, SC1, SC0);
  and and_14 (and_14_out, OPC0, SC1, SC0);
  and and_15 (and_15_out, not_3_out, not_4_out, not_5_out);
  and and_16 (and_16_out, not_1_out, SC1, SC0);
  and and_17 (and_17_out, OPC0, SC1, SC0);
  and and_18 (and_18_out, not_3_out, not_4_out, SC0);
  and and_19 (and_19_out, SC2, not_5_out);
  and and_20 (C11, OPC1, not_2_out, SC1, SC0);
  and and_21 (C12, not_2_out, SC2, SC0);
  and and_22 (C13, OPC0, SC2, SC0);
  and and_23 (C14, OPC1, OPC0, SC1, SC0);
  and and_24 (C15, OPC1, not_2_out, SC1, SC0);
  or or_1 (C3, and_4_out, and_5_out);
  or or_2 (C4, and_6_out, and_7_out, and_8_out);
  or or_3 (C5, and_9_out, and_10_out);
  or or_4 (C8, and_13_out, and_14_out);
  or or_5 (C9, and_15_out, and_16_out, and_17_out);
  or or_6 (C10, and_18_out, and_19_out);
endmodule
